# Fritzing sketch circuit (saved by Fritzing 0.9.3b)

parts:
  Part1 = Arduino Nano (Rev3.0) (ICSP)
  HC-SR04_Sensor_1 = HC-SR04 Ultrasonic Distance Sensor
  U1 = Vibration Motor- ROB-08449 [package=vibe-motor-10mm]
  Part2 = Bluetooth HC-05 Macho
  U2 = LIPO-2000mAh [package=lipo-2000]

nets:
  GND: Part1.GND, HC-SR04_Sensor_1.ECHO, U1.-, Part2.GND, U2.-
  N1: Part1.D2, Part2.State
  N2: Part1.D3, Part2.TXD
  N3: Part1.D4, Part2.RXD
  N4: Part1.D5, U1.+
  N5: Part1.D9, HC-SR04_Sensor_1.TRIG
  N6: Part1.D10, HC-SR04_Sensor_1.GND
  N7: Part1.VIN, Part1.A0, U2.+
  VCC: Part1.5V, HC-SR04_Sensor_1.VCC, Part2.VCC
